# Fritzing sketch pong (saved by Fritzing 0.9.3b)
breadboards: 2

parts:
  Part1 = Arduino Uno (Rev3) - ICSP
  Part2 = Arduino Uno (Rev3)
  U1 = POT [package=pot_mammoth]
  U2 = POT [package=pot_mammoth]
  U3 = 74HC595 SMD [package="SO16 [SMD]"]
  U4 = 74HC595 SMD [package="SO16 [SMD]"]
  Disp1 = LBT2088AH [part_number=LBT2088AH]

nets:
  N1: Part1.A4/SDA, Part2.A4/SDA
  N2: Part1.A5/SCL, Part2.A5/SCL
  N3: Part1.D11_PWM/MOSI, U4.SH_CP
  N4: Part1.D12/MISO, U4.ST_CP
  N5: Part1.D13/SCK, U4.DS
  GND: Part1.GND, Part2.GND, U1.S, U2.S, U3.GND, U3.OE, U4.GND, U4.OE
  N6: Part1.D2, U3.DS
  N7: Part1.D4, U3.ST_CP
  VCC: Part1.5V, U3.MR, U3.VCC, U4.MR, U4.VCC
  N8: Part2.A0, U2.A
  N9: Part2.A1, U1.A
  N10: Part2.5V, U2.E
  N11: U3.Q1, Disp1.pin_7
  N12: U3.Q2, Disp1.pin_4
  N13: U3.Q3, Disp1.pin1
  N14: U3.Q5, Disp1.pin_10
  N15: U3.Q6, Disp1.pin_13
  N16: U3.Q7, Disp1.pin_16
  N17: U4.Q1, Disp1.pin_5
  N18: U4.Q2, Disp1.pin2
  N19: U4.Q4, Disp1.pin_9
  N20: U4.Q5, Disp1.pin_12
  N21: U4.Q6, Disp1.pin_15
  N22: U4.Q0, Disp1.pin_8
